// Logisim project 8bitCPU.circ as structural Verilog: 7 circuits, main circuit CU
module CU (
  input  [7:0] OP,
  output ARWrite,
  output AR,
  output RegDst,
  output RegWrite,
  output RegData,
  output MemWrite,
  output [3:0] ALU_OP,
  output [1:0] NPC_OP
);

  wire and_2_out, and_3_out, and_4_out, and_6_out, and_7_out, not_1_out, not_2_out, not_3_out, not_4_out,
       not_5_out, not_6_out, not_7_out, not_8_out, not_9_out, not_10_out, not_11_out, not_12_out, not_13_out,
       not_14_out, not_15_out;

  not not_1 (not_1_out, OP[6]);
  not not_2 (not_2_out, OP[1]);
  not not_3 (not_3_out, OP[6]);
  not not_4 (not_4_out, OP[3]);
  not not_5 (not_5_out, OP[7]);
  not not_6 (not_6_out, OP[7]);
  not not_7 (not_7_out, OP[1]);
  not not_8 (not_8_out, OP[6]);
  not not_9 (not_9_out, OP[6]);
  not not_10 (not_10_out, OP[6]);
  not not_11 (not_11_out, OP[6]);
  not not_12 (not_12_out, OP[6]);
  not not_13 (not_13_out, OP[1]);
  not not_14 (not_14_out, OP[1]);
  not not_15 (not_15_out, OP[2]);
  and and_1 (ARWrite, not_1_out, OP[3]);
  and and_2 (and_2_out, OP[6], OP[3], not_2_out);
  and and_3 (and_3_out, OP[7], not_3_out, not_4_out);
  and and_4 (and_4_out, not_5_out, OP[6]);
  or or_1 (RegData, not_6_out, not_7_out);
  and and_5 (MemWrite, not_8_out, OP[2]);
  or or_2 (ALU_OP[3], not_9_out, OP[5], OP[7]);
  or or_3 (ALU_OP[2], not_10_out, OP[4], OP[7]);
  or or_4 (ALU_OP[1], not_11_out, OP[3], OP[7]);
  or or_5 (ALU_OP[0], not_12_out, OP[2], OP[7]);
  and and_6 (and_6_out, OP[6], OP[2], not_13_out);
  and and_7 (and_7_out, OP[6], OP[3], not_14_out);
  and and_8 (NPC_OP[0], OP[7], OP[6], not_15_out);
  or or_6 (AR, and_2_out, and_3_out);
  or or_7 (RegWrite, OP[1], and_4_out);
  or or_8 (NPC_OP[1], and_6_out, and_7_out);

  assign RegDst = OP[1];
endmodule

module NPC (
  input  [15:0] PC,
  input  [15:0] AR,
  input  Z,
  input  AR_2,
  input  [1:0] NPC_OP,
  output [15:0] NPC
);

  wire not_1_out;
  wire [15:0] adder_1_out, multiplexer_1_out, multiplexer_2_out;

  not not_1 (not_1_out, AR_2);
  Adder #(.width(16)) adder_1 (.a(PC), .b({16{1'b0}}), .out(adder_1_out), .cin(not_1_out));  // open: cout
  Multiplexer #(.width(16), .enable("false")) multiplexer_1 (
    .in0(adder_1_out), .in1(AR), .out(multiplexer_1_out), .sel(Z));
  Multiplexer #(.width(16), .enable("false")) multiplexer_2 (
    .in0(AR), .in1(adder_1_out), .out(multiplexer_2_out), .sel(Z));
  Multiplexer #(.select(2), .width(16), .enable("false")) multiplexer_3 (
    .in0(adder_1_out), .in1(AR), .in2(multiplexer_1_out), .in3(multiplexer_2_out), .out(NPC), .sel(NPC_OP));
endmodule

module ALU_OP_Decoder (
  input  [3:0] ALU_OP,
  output [7:0] Out
);

  wire and_1_out, and_2_out, and_3_out, and_4_out, and_5_out, and_6_out, and_7_out, and_8_out, not_1_out,
       not_2_out, not_4_out, not_5_out, not_6_out, not_7_out, not_8_out, not_9_out, not_10_out, not_11_out,
       not_12_out;

  not not_1 (not_1_out, ALU_OP[2]);
  not not_2 (not_2_out, ALU_OP[1]);
  and and_1 (and_1_out, ALU_OP[2], ALU_OP[0]);
  and and_2 (and_2_out, ALU_OP[2], ALU_OP[1]);
  not not_3 (Out[5], ALU_OP[2]);
  not not_4 (not_4_out, ALU_OP[2]);
  not not_5 (not_5_out, ALU_OP[3]);
  not not_6 (not_6_out, ALU_OP[1]);
  not not_7 (not_7_out, ALU_OP[0]);
  not not_8 (not_8_out, ALU_OP[1]);
  not not_9 (not_9_out, ALU_OP[2]);
  not not_10 (not_10_out, ALU_OP[3]);
  not not_11 (not_11_out, ALU_OP[2]);
  not not_12 (not_12_out, ALU_OP[1]);
  and and_3 (and_3_out, not_1_out, ALU_OP[1], ALU_OP[0]);
  and and_4 (and_4_out, ALU_OP[2], not_2_out);
  or or_1 (Out[6], and_1_out, and_2_out, ALU_OP[3]);
  and and_5 (and_5_out, not_4_out, ALU_OP[0]);
  and and_6 (and_6_out, ALU_OP[1], ALU_OP[0]);
  and and_7 (and_7_out, not_5_out, not_6_out, not_7_out);
  and and_8 (and_8_out, ALU_OP[2], not_8_out, ALU_OP[0]);
  and and_9 (Out[2], not_9_out, ALU_OP[1], ALU_OP[0]);
  and and_10 (Out[1], not_10_out, not_11_out, not_12_out, ALU_OP[0]);
  or or_2 (Out[7], and_3_out, and_4_out);
  or or_3 (Out[4], and_5_out, and_6_out);
  or or_4 (Out[3], and_7_out, and_8_out);

  assign Out[0] = 1'b0;
endmodule

module ALU (
  input  [7:0] AC,
  input  [7:0] R,
  input  [3:0] OP,
  output Z,
  output [7:0] Out
);

  wire Cin, S6;
  wire [1:0] S1_S0, S3_S2, S5_S4;
  wire [7:0] adder_1_out, and_1_out, multiplexer_1_out, multiplexer_2_out, multiplexer_3_out, not_1_out,
       not_2_out, not_3_out, or_1_out, xor_1_out;

  ALU_OP_Decoder alu_op_decoder_1 (.ALU_OP(OP), .Out({Cin, S6, S5_S4, S3_S2, S1_S0}));
  assign not_1_out = ~AC;  // NOT_Gate not_1, 8 bits wide
  assign not_2_out = ~R;  // NOT_Gate not_2, 8 bits wide
  Multiplexer #(.select(2), .width(8), .enable("false")) multiplexer_1 (
    .in0(AC), .in1(not_1_out), .in2({8{1'b0}}), .in3({8{1'b1}}), .out(multiplexer_1_out), .sel(S1_S0));
  Multiplexer #(.select(2), .width(8), .enable("false")) multiplexer_2 (
    .in0(R), .in1(not_2_out), .in2({8{1'b0}}), .in3({8{1'b1}}), .out(multiplexer_2_out), .sel(S3_S2));
  assign and_1_out = multiplexer_1_out & multiplexer_2_out;  // AND_Gate and_1, 8 bits wide
  assign or_1_out = multiplexer_1_out | multiplexer_2_out;  // OR_Gate or_1, 8 bits wide
  assign xor_1_out = multiplexer_1_out ^ multiplexer_2_out;  // XOR_Gate xor_1, 8 bits wide
  assign not_3_out = ~multiplexer_1_out;  // NOT_Gate not_3, 8 bits wide
  Adder adder_1 (.a(multiplexer_1_out), .b(multiplexer_2_out), .out(adder_1_out), .cin(Cin));  // open: cout
  Multiplexer #(.select(2), .width(8), .enable("false")) multiplexer_3 (
    .in0(and_1_out), .in1(or_1_out), .in2(xor_1_out), .in3(not_3_out), .out(multiplexer_3_out), .sel(S5_S4));
  Comparator comparator_1 (.a({8{1'b0}}), .b(AC), .eq(Z));  // open: gt, lt
  Multiplexer #(.width(8), .enable("false")) multiplexer_4 (
    .in0(adder_1_out), .in1(multiplexer_3_out), .out(Out), .sel(S6));
endmodule

module Regs (
  input  [7:0] InFromReg,
  input  [7:0] InFromAdd,
  input  RegData,
  input  RegDst,
  input  RegWrite,
  input  CLK,
  input  rst,
  output [7:0] AC,
  output [7:0] R
);

  wire and_1_out, and_2_out, decoder_1_out0, decoder_1_out1, not_1_out, not_2_out;
  wire [7:0] multiplexer_1_out;

  Multiplexer #(.width(8), .enable("false")) multiplexer_1 (
    .in0(InFromReg), .in1(InFromAdd), .out(multiplexer_1_out), .sel(not_1_out));
  not not_1 (not_1_out, RegData);
  Decoder #(.enable("false")) decoder_1 (.out0(decoder_1_out0), .out1(decoder_1_out1), .sel(not_2_out));
  not not_2 (not_2_out, RegDst);
  and and_1 (and_1_out, RegWrite, decoder_1_out0);
  and and_2 (and_2_out, RegWrite, decoder_1_out1);
  Register register_1 (.D(multiplexer_1_out), .en(and_1_out), .Q(AC), .clk(CLK), .clr(rst));
  Register register_2 (.D(multiplexer_1_out), .en(and_2_out), .Q(R), .clk(CLK), .clr(rst));
endmodule

module ARG (
  input  [7:0] AC,
  input  [7:0] R,
  output [15:0] out_3
);

  Adder #(.width(16)) adder_1 (.a({AC, {8{1'b0}}}), .b({{8{1'b0}}, R}), .out(out_3));  // open: cin, cout
endmodule

module CPU (
  input  rst,
  output [15:0] PC_value,
  output [7:0] IR_value,
  output [7:0] AC_value,
  output [7:0] R_value,
  output [15:0] NPC_value,
  output [7:0] R_value_2
);

  wire alu_1_z, clock_1_out, cu_1_ar, cu_1_arwrite, cu_1_memwrite, cu_1_regdata, cu_1_regdst, cu_1_regwrite,
       not_1_out, not_2_out;
  wire [1:0] cu_1_npc_op;
  wire [3:0] cu_1_alu_op;
  wire [7:0] controlled_buffer_3_out, multiplexer_1_out, ram_1_data;
  wire [15:0] AR_q, arg_1_out_3, controlled_buffer_1_out;

  Clock clock_1 (.out(clock_1_out));
  Register #(.width(16)) PC (.D(NPC_value), .Q(PC_value), .clk(clock_1_out), .clr(rst));  // open: en
  NPC npc_1 (.PC(PC_value), .AR(AR_q), .Z(alu_1_z), .AR_2(cu_1_ar), .NPC_OP(cu_1_npc_op), .NPC(NPC_value));
  Hex_Digit_Display hex_digit_display_1 (.value(NPC_value[15:12]));  // open: dp
  Hex_Digit_Display hex_digit_display_2 (.value(NPC_value[11:8]));  // open: dp
  assign controlled_buffer_1_out = not_1_out ? PC_value : 16'bz;  // Controlled_Buffer controlled_buffer_1
  assign controlled_buffer_1_out = cu_1_ar ? AR_q : 16'bz;  // Controlled_Buffer controlled_buffer_2
  not not_1 (not_1_out, cu_1_ar);
  Hex_Digit_Display hex_digit_display_3 (.value(NPC_value[7:4]));  // open: dp
  Hex_Digit_Display hex_digit_display_4 (.value(NPC_value[3:0]));  // open: dp
  Hex_Digit_Display hex_digit_display_5 (.value(PC_value[15:12]));  // open: dp
  Hex_Digit_Display hex_digit_display_6 (.value(PC_value[11:8]));  // open: dp
  Hex_Digit_Display hex_digit_display_7 (.value(PC_value[7:4]));  // open: dp
  RAM #(.addrWidth(16)) ram_1 (
    .addr(controlled_buffer_1_out), .data(ram_1_data), .clk(clock_1_out), .ld(not_2_out), .clr(rst));  // open: sel
  Hex_Digit_Display hex_digit_display_8 (.value(PC_value[3:0]));  // open: dp
  Register IR (.D(multiplexer_1_out), .Q(IR_value), .clk(clock_1_out), .clr(rst));  // open: en
  Multiplexer #(.width(8), .enable("false")) multiplexer_1 (
    .in0(ram_1_data), .in1({8{1'b0}}), .out(multiplexer_1_out), .sel(cu_1_ar));
  assign controlled_buffer_3_out = cu_1_ar ? AC_value : 8'bz;  // Controlled_Buffer controlled_buffer_3
  assign ram_1_data = cu_1_regdata ? controlled_buffer_3_out : 8'bz;  // Controlled_Buffer controlled_buffer_4
  Hex_Digit_Display hex_digit_display_9 (.value(IR_value[3:0]));  // open: dp
  Hex_Digit_Display hex_digit_display_10 (.value(IR_value[7:4]));  // open: dp
  CU cu_1 (
    .OP(IR_value), .ARWrite(cu_1_arwrite), .AR(cu_1_ar), .RegDst(cu_1_regdst), .RegWrite(cu_1_regwrite),
    .RegData(cu_1_regdata), .MemWrite(cu_1_memwrite), .ALU_OP(cu_1_alu_op), .NPC_OP(cu_1_npc_op));
  Regs regs_1 (
    .InFromReg(R_value_2), .InFromAdd(ram_1_data), .RegData(cu_1_regdata), .RegDst(cu_1_regdst),
    .RegWrite(cu_1_regwrite), .CLK(clock_1_out), .rst(rst), .AC(AC_value), .R(R_value));
  not not_2 (not_2_out, cu_1_memwrite);
  ARG arg_1 (.AC(AC_value), .R(R_value), .out_3(arg_1_out_3));
  Hex_Digit_Display hex_digit_display_11 (.value(AC_value[7:4]));  // open: dp
  Register #(.width(16)) AR (.D(arg_1_out_3), .en(cu_1_arwrite), .Q(AR_q), .clk(clock_1_out), .clr(rst));
  Hex_Digit_Display hex_digit_display_12 (.value(AC_value[3:0]));  // open: dp
  ALU alu_1 (.AC(AC_value), .R(R_value), .OP(cu_1_alu_op), .Z(alu_1_z), .Out(R_value_2));
  Hex_Digit_Display hex_digit_display_13 (.value(R_value[7:4]));  // open: dp
  Hex_Digit_Display hex_digit_display_14 (.value(R_value[3:0]));  // open: dp
endmodule
